# Fritzing sketch Cytis (saved by Fritzing 0.9.9b)
breadboards: 1

parts:
  Part1 = Arduino Nano (Rev3.0)
  L1 = Solenoid
  L298N1 = L298N DC motor driver
  L2 = Solenoid
  Part2 = Bluetooth HM-10
  U2 = Voltage Regulator - 5V [package="TO220 [THT]"]  # not connected
  VCC1 = 4 x AAA Battery Mount
  Part3 = Soil Moisture Sensor

nets:
  N1: Part1.D1/TX, Part2.RXD
  N2: Part1.D0/RX, Part2.TXD
  N3: Part1.D2, L298N1.IN1
  N4: Part1.D3, L298N1.IN2
  N5: Part1.D4, L298N1.IN3
  N6: Part1.D5, L298N1.IN4
  GND: Part1.GND, L298N1.GND, Part2.GND, VCC1.-, Part3.GND
  VCC: Part1.5V, L298N1.5V#7, Part2.VCC, Part3.VCC
  N7: Part1.A0, Part3.SIG
  N8: L1.pin1, L298N1.OUT2
  N9: L1.pin2, L298N1.OUT1
  N10: L298N1.OUT3, L2.pin1
  N11: L298N1.OUT4, L2.pin2
  N12: L298N1.12V, VCC1.+
  N13: L298N1.5V#9, L298N1.ENA
  N14: L298N1.5V#10, L298N1.ENB

custom parts:
  L298N DC motor driver: 2x DC motor driver with 78M05 positive voltage regulator (7..35 V) L298N: max 46 V, 2 A Set 5 V Enable jumper to enable 5 V regultor (needed for the L298N) and +5 V output at screw terminal or supply external +5 V at screw terminal Set ENA and/or ENB to +5 V to enable motor permanently or supply ENA and/or ENB with PWM signal IN1 and IN2 set rotation directory for motor A (OUT1/OUT2) IN2 and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
